// Logisim project Booth.circ as structural Verilog: 1 circuit, main circuit main
module main (
  input  [3:0] multiplicand,
  input  [1:0] in_2,
  input  [3:0] multiplier,
  input  in_4,
  input  [2:0] in_5,
  input  [2:0] in_6,
  input  start,
  input  reset,
  input  in_9,
  output [7:0] out_10
);

  wire clk_out, comparator_1_eq, comparator_1_gt, not_1_out, not_2_out, Q_1_q;
  wire [1:0] adder_2_out, bit_extender_1_out, bit_extender_2_out, shifter_1_out;
  wire [2:0] counter_1_q;
  wire [3:0] adder_1_out, controlled_buffer_1_out, M_q, multiplexer_1_out, shifter_2_out, subtractor_1_out;

  Counter #(.max('h5), .ongoal("stay"), .width(3)) counter_1 (
    .clr(not_2_out), .load(not_1_out), .up(in_4), .clk(clk_out), .D(in_5), .Q(counter_1_q));  // open: count, carry
  not not_1 (not_1_out, start);
  Comparator #(.mode("unsigned"), .width(3)) comparator_1 (
    .a(counter_1_q), .b(in_6), .gt(comparator_1_gt), .eq(comparator_1_eq));  // open: lt
  assign controlled_buffer_1_out = comparator_1_eq ? multiplier : 4'bz;  // Controlled_Buffer controlled_buffer_1
  assign controlled_buffer_1_out = comparator_1_gt ? {multiplexer_1_out[0], out_10[3:1]} : 4'bz;  // Controlled_Buffer controlled_buffer_2
  not not_2 (not_2_out, reset);
  Clock clk (.out(clk_out));
  Register #(.width(4)) M (.D(multiplicand), .en(start), .clk(clk_out), .Q(M_q), .clr(not_2_out));
  Register #(.width(4)) A (.D(shifter_2_out), .en(start), .clk(clk_out), .Q(out_10[7:4]), .clr(not_2_out));
  Register #(.width(4)) Q (.D(controlled_buffer_1_out), .en(start), .clk(clk_out), .Q(out_10[3:0]), .clr(not_2_out));
  Register #(.width(1)) Q_1 (.D(out_10[0]), .en(start), .clk(clk_out), .Q(Q_1_q), .clr(not_2_out));
  Adder #(.width(4)) adder_1 (.a(M_q), .b(out_10[7:4]), .out(adder_1_out));  // open: cin, cout
  Subtractor #(.width(4)) subtractor_1 (.a(out_10[7:4]), .b(M_q), .out(subtractor_1_out));  // open: bin, bout
  assign bit_extender_1_out = {{1{1'b0}}, out_10[0]};  // Bit_Extender bit_extender_1
  assign bit_extender_2_out = {{1{1'b0}}, Q_1_q};  // Bit_Extender bit_extender_2
  // Probe on adder_2_out
  Shifter #(.width(2)) shifter_1 (.in(bit_extender_1_out), .\dist (in_9), .out(shifter_1_out));
  // Probe on multiplexer_1_out
  Multiplexer #(.select(2), .width(4)) multiplexer_1 (
    .in0(out_10[7:4]), .in1(adder_1_out), .in2(subtractor_1_out), .in3(out_10[7:4]), .out(multiplexer_1_out),
    .sel(adder_2_out));
  Adder #(.width(2)) adder_2 (.a(shifter_1_out), .b(bit_extender_2_out), .out(adder_2_out));  // open: cin, cout
  // Probe on shifter_2_out
  Shifter #(.shift("ar"), .width(4)) shifter_2 (.in(multiplexer_1_out), .\dist (in_2), .out(shifter_2_out));
endmodule
