// Logisim project AsynchronousCounter.circ as structural Verilog: 1 circuit, main circuit main
module main (
  input  reset,
  output A0,
  output A1,
  output A2,
  output A3
);

  wire clk_out, d_ff_1_qn, d_ff_2_qn, d_ff_3_qn, d_ff_4_qn;

  Clock clk (.out(clk_out));
  D_Flip_Flop d_ff_1 (.D(d_ff_1_qn), .clk(clk_out), .Q(A0), .Qn(d_ff_1_qn), .reset(reset));  // open: preset
  D_Flip_Flop d_ff_2 (.D(d_ff_2_qn), .clk(d_ff_1_qn), .Q(A1), .Qn(d_ff_2_qn), .reset(reset));  // open: preset
  D_Flip_Flop d_ff_3 (.D(d_ff_3_qn), .clk(d_ff_2_qn), .Q(A2), .Qn(d_ff_3_qn), .reset(reset));  // open: preset
  D_Flip_Flop d_ff_4 (.D(d_ff_4_qn), .clk(d_ff_3_qn), .Q(A3), .Qn(d_ff_4_qn), .reset(reset));  // open: preset
endmodule
