// Logisim project DFlipFlop.circ as structural Verilog: 1 circuit, main circuit main
module main (
  input  D,
  output Output
);

  wire clk_out, multiplexer_1_out, not_1_out;

  Clock clk (.out(clk_out));
  Multiplexer multiplexer_1 (.in0(multiplexer_1_out), .in1(D), .out(multiplexer_1_out), .sel(not_1_out));
  not not_1 (not_1_out, clk_out);
  Multiplexer multiplexer_2 (.in0(Output), .in1(multiplexer_1_out), .out(Output), .sel(clk_out));
endmodule
