// Logisim project Latch.circ as structural Verilog: 1 circuit, main circuit main
module main (
  input  D,
  input  S,
  output Output
);

  Multiplexer multiplexer_1 (.in0(Output), .in1(D), .out(Output), .sel(S));
endmodule
