// Logisim project MUX.circ as structural Verilog: 1 circuit, main circuit main
module main (
  input  S_prime,
  input  S,
  output out_3
);

  // Transmission_Gate transmission_1: pin names not known; wires that end beside it: 1'b1, S, S_prime, out_3
  // Transmission_Gate transmission_2: pin names not known; wires that end beside it: 1'b0, S_prime, S, out_3

  // Notes on the sheet:
  //   Input1
  //   Input2
endmodule
