// Logisim project SynchronousCounter.circ as structural Verilog: 1 circuit, main circuit main
module main (
  input  updown,
  input  reset,
  output A0,
  output A1,
  output A2,
  output A3
);

  wire adder_1_out, adder_2_cout, adder_2_out, adder_3_cout, adder_3_out, adder_4_cout, adder_4_out,
       adder_5_out, clk_out, not_1_out;

  not not_1 (not_1_out, updown);
  Adder #(.width(1)) adder_1 (.a(not_1_out), .b(updown), .out(adder_1_out));  // open: cin, cout
  Adder #(.width(1)) adder_2 (.a(A0), .b(adder_1_out), .out(adder_2_out), .cout(adder_2_cout));  // open: cin
  Adder #(.width(1)) adder_3 (.a(A1), .b(adder_2_cout), .out(adder_3_out), .cin(updown), .cout(adder_3_cout));
  Adder #(.width(1)) adder_4 (.a(A2), .b(adder_3_cout), .out(adder_4_out), .cin(updown), .cout(adder_4_cout));
  Adder #(.width(1)) adder_5 (.a(A3), .b(adder_4_cout), .out(adder_5_out), .cin(updown));  // open: cout
  Clock clk (.out(clk_out));
  D_Flip_Flop d_ff_1 (.D(adder_2_out), .clk(clk_out), .Q(A0), .reset(reset));  // open: Qn, preset
  D_Flip_Flop d_ff_2 (.D(adder_3_out), .clk(clk_out), .Q(A1), .reset(reset));  // open: Qn, preset
  D_Flip_Flop d_ff_3 (.D(adder_4_out), .clk(clk_out), .Q(A2), .reset(reset));  // open: Qn, preset
  D_Flip_Flop d_ff_4 (.D(adder_5_out), .clk(clk_out), .Q(A3), .reset(reset));  // open: Qn, preset
endmodule
