// Logisim project TransmissionGate.circ as structural Verilog: 1 circuit, main circuit main
module main (
  input  S_prime,
  input  \input ,
  input  S,
  output \output 
);

  // Transmission_Gate transmission_1: pin names not known; wires that end beside it: \input , S_prime, S_prime, S, \output 
endmodule
