// Logisim project project.circ as structural Verilog: 1 circuit, main circuit main
module main (
  input  reset
);

  wire and_1_out, and_2_out, and_3_out, and_4_out, and_5_out, clk_out, comparator_1_eq, comparator_1_gt,
       d_ff_1_q, decoder_1_out7, decoder_1_out8, decoder_1_out9, decoder_1_out10, decoder_1_out11,
       decoder_1_out12, decoder_1_out13, decoder_1_out14, decoder_1_out15, multiplexer_3_out, not_1_out,
       not_2_out, not_3_out, not_5_out, or_1_out, or_2_out, or_3_out, or_4_out, w1, w2, w3, w4, w5, w6, w7,
       w8;
  wire [3:0] bit_extender_1_out, PC_q, PC_q_2, PC_q_3, register_1_q, register_1_q_2, register_1_q_3,
       register_1_q_4;
  wire [11:0] adder_1_out, multiplexer_1_out, multiplexer_2_out;
  wire [15:0] adder_2_out, multiplexer_4_out, multiplexer_5_out, not_4_out, ram_1_dout, register_2_q;

  D_Flip_Flop d_ff_1 (.D(not_1_out), .clk(clk_out), .Q(d_ff_1_q), .reset(reset));  // open: Qn, preset
  not not_1 (not_1_out, d_ff_1_q);
  Clock clk (.out(clk_out));
  or or_1 (or_1_out, and_4_out, w6, and_5_out, d_ff_1_q);
  Hex_Digit_Display hex_digit_display_1 (.value(PC_q_3));  // open: dp
  Hex_Digit_Display hex_digit_display_2 (.value(PC_q_2));  // open: dp
  or or_2 (or_2_out, and_5_out, w6, and_4_out);
  Adder #(.width(12)) adder_1 (
    .a({PC_q_3, PC_q_2, PC_q}), .b({12{1'b0}}), .out(adder_1_out), .cin(1'b1));  // open: cout
  Multiplexer #(.width(12)) multiplexer_1 (
    .in0(adder_1_out), .in1(register_2_q[11:0]), .out(multiplexer_1_out), .sel(or_2_out));
  and and_1 (and_1_out, or_1_out, w7);
  not not_2 (not_2_out, d_ff_1_q);
  Hex_Digit_Display hex_digit_display_3 (.value(PC_q));  // open: dp
  Register #(.width(12)) PC (
    .D(multiplexer_1_out), .en(and_1_out), .clk(clk_out), .Q({PC_q_3, PC_q_2, PC_q}), .clr(reset));
  Hex_Digit_Display hex_digit_display_4 (.value(multiplexer_2_out[11:8]));  // open: dp
  Multiplexer #(.width(12)) multiplexer_2 (
    .in0({PC_q_3, PC_q_2, PC_q}), .in1(register_2_q[11:0]), .out(multiplexer_2_out), .sel(d_ff_1_q));
  Hex_Digit_Display hex_digit_display_5 (.value(multiplexer_2_out[7:4]));  // open: dp
  Hex_Digit_Display hex_digit_display_6 (.value(multiplexer_2_out[3:0]));  // open: dp
  not not_3 (not_3_out, clk_out);
  and and_2 (and_2_out, w8, not_3_out, d_ff_1_q);
  Multiplexer multiplexer_3 (.in0(1'b0), .in1(1'b1), .out(multiplexer_3_out), .sel(w2));
  assign not_4_out = ~ram_1_dout;  // NOT_Gate not_4, 16 bits wide
  RAM #(.addrWidth(12), .asyncread("true"), .dataWidth(16)) ram_1 (
    .addr(multiplexer_2_out), .we(and_2_out), .oe(1'b1), .clk(clk_out),
    .din({register_1_q_4, register_1_q_3, register_1_q_2, register_1_q}), .dout(ram_1_dout));
  // Probe on multiplexer_4_out
  Multiplexer #(.width(16)) multiplexer_4 (
    .in0({register_1_q_4, register_1_q_3, register_1_q_2, register_1_q}), .in1({16{1'b0}}),
    .out(multiplexer_4_out), .sel(w1));
  Multiplexer #(.width(16)) multiplexer_5 (
    .in0(ram_1_dout), .in1(not_4_out), .out(multiplexer_5_out), .sel(multiplexer_3_out));
  // Probe on multiplexer_5_out
  // Probe on adder_2_out
  Adder #(.width(16)) adder_2 (
    .a(multiplexer_4_out), .b(multiplexer_5_out), .out(adder_2_out), .cin(multiplexer_3_out));  // open: cout
  or or_3 (or_3_out, w1, w2, w3);
  Register #(.width(16)) register_1 (
    .D(adder_2_out), .en(and_3_out), .clk(clk_out),
    .Q({register_1_q_4, register_1_q_3, register_1_q_2, register_1_q}), .clr(reset));
  and and_3 (and_3_out, or_3_out, d_ff_1_q);
  // Probe on ram_1_dout
  Hex_Digit_Display hex_digit_display_7 (.value(register_1_q_4));  // open: dp
  Register #(.width(16)) register_2 (.D(ram_1_dout), .en(not_2_out), .clk(clk_out), .Q(register_2_q), .clr(reset));
  Comparator #(.width(16)) comparator_1 (
    .a({register_1_q_4, register_1_q_3, register_1_q_2, register_1_q}), .b({16{1'b0}}), .gt(comparator_1_gt),
    .eq(comparator_1_eq));  // open: lt
  Hex_Digit_Display hex_digit_display_8 (.value(register_1_q_3));  // open: dp
  Hex_Digit_Display hex_digit_display_9 (.value(register_1_q_2));  // open: dp
  // Probe on register_2_q[11:0]
  Hex_Digit_Display hex_digit_display_10 (.value(bit_extender_1_out));  // open: dp
  assign bit_extender_1_out = {{3{1'b0}}, d_ff_1_q};  // Bit_Extender bit_extender_1
  or or_4 (or_4_out, comparator_1_gt, comparator_1_eq);
  not not_5 (not_5_out, comparator_1_eq);
  Hex_Digit_Display hex_digit_display_11 (.value(register_1_q));  // open: dp
  Hex_Digit_Display hex_digit_display_12 (.value(register_2_q[15:12]));  // open: dp
  Decoder #(.enable("false"), .select(4)) decoder_1 (
    .out0(w1), .out1(w8), .out2(w3), .out3(w2), .out4(w6), .out5(w4), .out6(w5), .out7(decoder_1_out7),
    .out8(decoder_1_out8), .out9(decoder_1_out9), .out10(decoder_1_out10), .out11(decoder_1_out11),
    .out12(decoder_1_out12), .out13(decoder_1_out13), .out14(decoder_1_out14), .out15(decoder_1_out15),
    .sel(register_2_q[15:12]));
  and and_4 (and_4_out, or_4_out, w4);
  and and_5 (and_5_out, not_5_out, w5);
  nor nor_1 (w7, decoder_1_out7, decoder_1_out8, decoder_1_out9, decoder_1_out10, decoder_1_out11, decoder_1_out12, decoder_1_out13, decoder_1_out14, decoder_1_out15);

  // Notes on the sheet:
  //   Program Counter
  //   Memory Address
  //   Accumulator Value
  //   Machine State
  //   opcode
  //   1: Execution
  //   0: Instruction Fetch
endmodule
